# Fritzing sketch LCD1602Clock (saved by Fritzing 0.9.3b)
breadboards: 1

parts:
  부품1 = Arduino Nano (Rev3.0)
  부품2 = LCD1602-I2C
  X1 = USB Connectors [package=usb-microb]
  J1 = Piezo Speaker  # not connected
  RHT1 = Humidity and Temperature Sensor RHT03
  PCB2 = RTC_DS1302_module  # not connected

nets:
  N1: 부품1.RESET, 부품1.5V
  N2: 부품1.D2, 부품1.A0
  N3: 부품1.A7, X1.VBUS
  N4: 부품1.A6, RHT1.GND_2
  VCC: 부품1.D13/SCK, 부품2.VCC, RHT1.Vcc

custom parts:
  LCD1602-I2C: A standard character display, usually with 2x16 characters. Comes in many colors with LCM1602 IIC attached.
  RTC_DS1302_module: Arduino module DS1302 SPI Real Time Clock
